# Fritzing sketch One Relay AoG (saved by Fritzing 0.9.3b)

parts:
  WeMos_D1_Mini1 = WeMos D1 Mini
  KY-1 = Keyes Relay [package=THT]

nets:
  N1: WeMos_D1_Mini1.3V3, KY-1.power
  N2: WeMos_D1_Mini1.D6, KY-1.signal
  N3: WeMos_D1_Mini1.G, KY-1.ground

custom parts:
  Keyes Relay: The Keyes 5V relay module is suitable for SCM development, home appliance control. It uses a 5V~12V TIL control signal which can control DC / AC signal.
